// Logisim project circuit.circ as structural Verilog: 3 circuits, main circuit main
module main (
);

  wire and_1_out, central_processing_jmp, central_processing_jz, CLK_out, or_1_out, R_out;
  wire [3:0] central_processing_f;
  wire [7:0] central_processing_j_a, central_processing_o, counter_1_q;
  wire [15:0] program_memory_data;

  Button CLK (.out(CLK_out));
  Button R (.out(R_out));
  ROM #(.dataWidth(16)) program_memory (.addr(counter_1_q), .data(program_memory_data));
  Counter counter_1 (
    .load(or_1_out), .D(central_processing_j_a), .count(1'b1), .Q(counter_1_q), .up(1'b1), .clk(CLK_out),
    .clr(R_out));  // open: carry
  LedBar O (
    .led0(central_processing_o[7]), .led1(central_processing_o[6]), .led2(central_processing_o[5]),
    .led3(central_processing_o[4]), .led4(central_processing_o[3]), .led5(central_processing_o[2]),
    .led6(central_processing_o[1]), .led7(central_processing_o[0]));
  // Probe on central_processing_o
  cpu central_processing (
    .I(program_memory_data), .CLK(CLK_out), .O(central_processing_o), .F(central_processing_f),
    .J_a(central_processing_j_a), .JMP(central_processing_jmp), .JZ(central_processing_jz));
  or or_1 (or_1_out, central_processing_jmp, and_1_out);
  and and_1 (and_1_out, central_processing_f[1], central_processing_jz);

  // Notes on the sheet:
  //   contents of program_memory (hex, n*v repeats v):
  //   3b 13c 43a 10 19 3 1d 14 23 33f 8a
endmodule

module alu (
  input  [7:0] A,
  input  [7:0] B,
  input  [2:0] OP,
  output [7:0] O,
  output [3:0] F
);

  wire xnor_1_out, xnor_2_out, xor_1_out;
  wire [7:0] adder_1_out, and_1_out, negator_1_out, not_1_out, or_1_out, shifter_1_out, shifter_2_out,
       subtractor_1_out;

  assign and_1_out = A & B;  // AND_Gate and_1, 8 bits wide
  assign or_1_out = A | B;  // OR_Gate or_1, 8 bits wide
  assign not_1_out = ~A;  // NOT_Gate not_1, 8 bits wide
  Negator negator_1 (.in(A), .out(negator_1_out));
  Adder adder_1 (.a(A), .b(B), .out(adder_1_out), .cout(F[2]));  // open: cin
  Subtractor subtractor_1 (.a(A), .b(B), .out(subtractor_1_out));  // open: bin, bout
  Shifter #(.shift("ar")) shifter_1 (.in(A), .\dist (B[2:0]), .out(shifter_1_out));
  Shifter shifter_2 (.in(A), .\dist (B[2:0]), .out(shifter_2_out));
  Multiplexer #(.enable("true"), .select(3), .width(8)) multiplexer_1 (
    .in0(and_1_out), .in1(or_1_out), .in2(not_1_out), .in3(negator_1_out), .in4(adder_1_out),
    .in5(subtractor_1_out), .in6(shifter_1_out), .in7(shifter_2_out), .out({F[0], O[6:0]}), .sel(OP),
    .en(1'b1));
  nor nor_1 (F[1], O[0], O[1], O[2], O[3], O[4], O[5], O[6], F[0]);
  xnor xnor_1 (xnor_1_out, A[7], B[7]);
  xor xor_1 (xor_1_out, A[7], B[7]);
  xnor xnor_2 (xnor_2_out, F[2], xnor_1_out);
  xor xor_2 (F[3], xnor_2_out, xor_1_out);

  assign O[7] = F[0];
endmodule

module cpu (
  input  [15:0] I,
  input  CLK,
  output [7:0] O,
  output [3:0] F,
  output [7:0] J_a,
  output JMP,
  output JZ
);

  wire decoder_1_out0, decoder_1_out1, decoder_1_out2, decoder_1_out3, decoder_1_out4, decoder_1_out5,
       decoder_1_out6, decoder_1_out7, decoder_2_out1;
  wire [1:0] register_3_q_3;
  wire [2:0] register_3_q, register_3_q_2;
  wire [7:0] arithmetic_and_logic_o, demultiplexer_1_out0, demultiplexer_1_out1, demultiplexer_1_out2,
       demultiplexer_1_out3, demultiplexer_1_out4, demultiplexer_1_out5, demultiplexer_1_out6,
       demultiplexer_1_out7, memory_dout, register_1_q, register_2_q, register_4_q, register_5_q,
       register_6_q, register_7_q;

  Demultiplexer #(.enable("true"), .select(3), .width(8)) demultiplexer_1 (
    .out0(demultiplexer_1_out0), .out1(demultiplexer_1_out1), .out2(demultiplexer_1_out2),
    .out3(demultiplexer_1_out3), .out4(demultiplexer_1_out4), .out5(demultiplexer_1_out5),
    .out6(demultiplexer_1_out6), .out7(demultiplexer_1_out7), .in(O), .sel(I[2:0]), .en(1'b1));
  Decoder #(.select(3)) decoder_1 (
    .out0(decoder_1_out0), .out1(decoder_1_out1), .out2(decoder_1_out2), .out3(decoder_1_out3),
    .out4(decoder_1_out4), .out5(decoder_1_out5), .out6(decoder_1_out6), .out7(decoder_1_out7), .sel(I[2:0]),
    .en(1'b1));
  Decoder #(.select(2)) decoder_2 (
    .out1(decoder_2_out1), .out2(JMP), .out3(JZ), .sel(I[7:6]), .en(1'b1));  // open: out0
  Register register_1 (.D(demultiplexer_1_out0), .en(decoder_1_out0), .Q(register_1_q), .clk(CLK));  // open: clr
  Register register_2 (.D(demultiplexer_1_out1), .en(decoder_1_out1), .Q(register_2_q), .clk(CLK));  // open: clr
  Register register_3 (
    .D(demultiplexer_1_out2), .en(decoder_1_out2), .Q({register_3_q_3, register_3_q_2, register_3_q}),
    .clk(CLK));  // open: clr
  Register register_4 (.D(demultiplexer_1_out3), .en(decoder_1_out3), .Q(register_4_q), .clk(CLK));  // open: clr
  Register register_5 (.D(demultiplexer_1_out4), .en(decoder_1_out4), .Q(register_5_q), .clk(CLK));  // open: clr
  Register register_6 (.D(demultiplexer_1_out5), .en(decoder_1_out5), .Q(register_6_q), .clk(CLK));  // open: clr
  Register register_7 (.D(demultiplexer_1_out6), .en(decoder_1_out6), .Q(register_7_q), .clk(CLK));  // open: clr
  Register register_8 (.D(demultiplexer_1_out7), .en(decoder_1_out7), .Q(J_a), .clk(CLK));  // open: clr
  RAM memory (.addr(register_1_q), .we(decoder_2_out1), .oe(1'b1), .clk(CLK), .din(register_2_q), .dout(memory_dout));
  alu arithmetic_and_logic (.A(register_1_q), .B(register_2_q), .OP(register_3_q), .O(arithmetic_and_logic_o), .F(F));
  Multiplexer #(.enable("true"), .select(3), .width(8)) multiplexer_1 (
    .in0(arithmetic_and_logic_o), .in1({register_3_q_3, register_3_q_2, register_3_q}), .in2(register_4_q),
    .in3(register_5_q), .in4(register_6_q), .in5(memory_dout), .in6(register_7_q), .in7(I[15:8]), .out(O),
    .sel(I[5:3]), .en(1'b1));
endmodule
