// Logisim project newnewnew.circ as structural Verilog: 3 circuits, main circuit main
module main (
  input  [7:0] A,
  input  [7:0] B,
  input  in_3,
  input  [1:0] OP,
  input  [15:0] I,
  input  CLK,
  output [7:0] O,
  output [3:0] F,
  output [7:0] O_w,
  output [3:0] F_alu,
  output [7:0] J_a,
  output J_e,
  output J_m
);

  wire and_2_out, and_3_out, clock_1_out, cpu_1_j_e, cpu_1_j_m, decoder_1_out0, decoder_1_out1,
       decoder_1_out2, decoder_1_out3, decoder_2_out1, not_2_out, xnor_1_out, xnor_2_out, xor_1_out,
       xor_3_out;
  wire [3:0] cpu_1_f_alu;
  wire [7:0] adder_1_out, alu_1_o, and_1_out, counter_1_q, cpu_1_j_a, cpu_1_o_w, demultiplexer_1_out0,
       demultiplexer_1_out1, demultiplexer_1_out2, demultiplexer_1_out3, not_1_out, ram_1_dout, register_1_q,
       register_2_q, register_3_q, shifter_1_out;
  wire [15:0] rom_1_data;

  assign and_1_out = A & B;  // AND_Gate and_1, 8 bits wide
  assign not_1_out = ~A;  // NOT_Gate not_1, 8 bits wide
  Adder adder_1 (.a(A), .b(B), .out(adder_1_out), .cout(F[2]));  // open: cin
  Shifter #(.shift("ar")) shifter_1 (.in(A), .\dist (B[2:0]), .out(shifter_1_out));
  Demultiplexer #(.select(2), .width(8)) demultiplexer_1 (
    .out0(demultiplexer_1_out0), .out1(demultiplexer_1_out1), .out2(demultiplexer_1_out2),
    .out3(demultiplexer_1_out3), .in(O_w), .sel(I[3:2]));
  Decoder #(.enable("false"), .select(2)) decoder_1 (
    .out0(decoder_1_out0), .out1(decoder_1_out1), .out2(decoder_1_out2), .out3(decoder_1_out3), .sel(I[3:2]));
  Decoder #(.enable("false"), .select(2)) decoder_2 (
    .out1(decoder_2_out1), .out2(J_e), .out3(J_m), .sel(I[7:6]));  // open: out0
  Multiplexer #(.select(2), .width(8)) multiplexer_1 (
    .in0(and_1_out), .in1(not_1_out), .in2(adder_1_out), .in3(shifter_1_out), .out({F[0], O[6:0]}), .sel(OP));
  Register register_1 (.D(demultiplexer_1_out0), .en(decoder_1_out0), .Q(register_1_q), .clk(CLK));  // open: clr
  Register register_2 (.D(demultiplexer_1_out1), .en(decoder_1_out1), .Q(register_2_q), .clk(CLK));  // open: clr
  Register register_3 (.D(demultiplexer_1_out2), .en(decoder_1_out2), .Q(register_3_q), .clk(CLK));  // open: clr
  Register register_4 (.D(demultiplexer_1_out3), .en(decoder_1_out3), .Q(J_a), .clk(CLK));  // open: clr
  nor nor_1 (F[1], O[0], O[1], O[2], O[3], O[4], O[5], O[6], F[0]);
  xnor xnor_1 (xnor_1_out, A[7], B[7]);
  xor xor_1 (xor_1_out, A[7], B[7]);
  RAM ram_1 (.addr(register_1_q), .we(decoder_2_out1), .oe(1'b1), .clk(CLK), .din(register_2_q), .dout(ram_1_dout));
  xnor xnor_2 (xnor_2_out, F[2], xnor_1_out);
  xor xor_2 (F[3], xnor_2_out, xor_1_out);
  alu alu_1 (.A(register_1_q), .B(register_2_q), .OP(I[1:0]), .O(alu_1_o), .F(F_alu));
  Multiplexer #(.select(2), .width(8)) multiplexer_2 (
    .in0(alu_1_o), .in1(ram_1_dout), .in2(register_3_q), .in3(I[15:8]), .out(O_w), .sel(I[5:4]));
  Clock clock_1 (.out(clock_1_out));
  ROM #(.dataWidth(16)) rom_1 (.addr(counter_1_q), .data(rom_1_data));
  Counter counter_1 (
    .load(xor_3_out), .D(cpu_1_j_a), .count(1'b1), .Q(counter_1_q), .up(1'b1), .clk(clock_1_out), .clr(in_3));  // open: carry
  // Probe on cpu_1_o_w
  cpu cpu_1 (
    .I(rom_1_data), .CLK(clock_1_out), .O_w(cpu_1_o_w), .F_alu(cpu_1_f_alu), .J_a(cpu_1_j_a),
    .J_e(cpu_1_j_e), .J_m(cpu_1_j_m));
  // Probe on cpu_1_f_alu
  and and_2 (and_2_out, cpu_1_j_e, not_2_out);
  not not_2 (not_2_out, cpu_1_j_m);
  xor xor_3 (xor_3_out, and_2_out, and_3_out);
  and and_3 (and_3_out, cpu_1_f_alu[1], cpu_1_j_m);

  assign O[7] = F[0];

  // Notes on the sheet:
  //   contents of rom_1 (hex, n*v repeats v):
  //   30 134 2 1 9 30 2 24 23c 98
endmodule

module alu (
  input  [7:0] A,
  input  [7:0] B,
  input  [1:0] OP,
  output [7:0] O,
  output [3:0] F
);

  wire xnor_1_out, xnor_2_out, xor_1_out;
  wire [7:0] adder_1_out, and_1_out, not_1_out, shifter_1_out;

  assign and_1_out = A & B;  // AND_Gate and_1, 8 bits wide
  assign not_1_out = ~A;  // NOT_Gate not_1, 8 bits wide
  Adder adder_1 (.a(A), .b(B), .out(adder_1_out), .cout(F[2]));  // open: cin
  Shifter #(.shift("ar")) shifter_1 (.in(A), .\dist (B[2:0]), .out(shifter_1_out));
  Multiplexer #(.select(2), .width(8)) multiplexer_1 (
    .in0(and_1_out), .in1(not_1_out), .in2(adder_1_out), .in3(shifter_1_out), .out({F[0], O[6:0]}), .sel(OP));
  nor nor_1 (F[1], O[0], O[1], O[2], O[3], O[4], O[5], O[6], F[0]);
  xnor xnor_1 (xnor_1_out, A[7], B[7]);
  xor xor_1 (xor_1_out, A[7], B[7]);
  xnor xnor_2 (xnor_2_out, F[2], xnor_1_out);
  xor xor_2 (F[3], xnor_2_out, xor_1_out);

  assign O[7] = F[0];
endmodule

module cpu (
  input  [15:0] I,
  input  CLK,
  output [7:0] O_w,
  output [3:0] F_alu,
  output [7:0] J_a,
  output J_e,
  output J_m
);

  wire decoder_1_out0, decoder_1_out1, decoder_1_out2, decoder_1_out3, decoder_2_out1;
  wire [7:0] alu_1_o, demultiplexer_1_out0, demultiplexer_1_out1, demultiplexer_1_out2, demultiplexer_1_out3,
       ram_1_dout, register_1_q, register_2_q, register_3_q;

  Demultiplexer #(.select(2), .width(8)) demultiplexer_1 (
    .out0(demultiplexer_1_out0), .out1(demultiplexer_1_out1), .out2(demultiplexer_1_out2),
    .out3(demultiplexer_1_out3), .in(O_w), .sel(I[3:2]));
  Decoder #(.enable("false"), .select(2)) decoder_1 (
    .out0(decoder_1_out0), .out1(decoder_1_out1), .out2(decoder_1_out2), .out3(decoder_1_out3), .sel(I[3:2]));
  Decoder #(.enable("false"), .select(2)) decoder_2 (
    .out1(decoder_2_out1), .out2(J_e), .out3(J_m), .sel(I[7:6]));  // open: out0
  Register register_1 (.D(demultiplexer_1_out0), .en(decoder_1_out0), .Q(register_1_q), .clk(CLK));  // open: clr
  Register register_2 (.D(demultiplexer_1_out1), .en(decoder_1_out1), .Q(register_2_q), .clk(CLK));  // open: clr
  Register register_3 (.D(demultiplexer_1_out2), .en(decoder_1_out2), .Q(register_3_q), .clk(CLK));  // open: clr
  Register register_4 (.D(demultiplexer_1_out3), .en(decoder_1_out3), .Q(J_a), .clk(CLK));  // open: clr
  RAM ram_1 (.addr(register_1_q), .we(decoder_2_out1), .oe(1'b1), .clk(CLK), .din(register_2_q), .dout(ram_1_dout));
  alu alu_1 (.A(register_1_q), .B(register_2_q), .OP(I[1:0]), .O(alu_1_o), .F(F_alu));
  Multiplexer #(.select(2), .width(8)) multiplexer_1 (
    .in0(alu_1_o), .in1(ram_1_dout), .in2(register_3_q), .in3(I[15:8]), .out(O_w), .sel(I[5:4]));
endmodule
